// Logisim project 3-8_line_decoder.circ as structural Verilog: 1 circuit, main circuit main
module main (
  input  A2,
  input  A1,
  input  A0,
  input  in_4
);

  wire and_1_out, and_2_out, and_3_out, and_4_out, and_5_out, and_6_out, and_7_out, and_8_out, not_1_out,
       not_2_out, not_3_out;

  not not_1 (not_1_out, A2);
  not not_2 (not_2_out, A1);
  not not_3 (not_3_out, A0);
  LED led_1 (.in(and_1_out));
  and and_1 (and_1_out, not_1_out, not_2_out, not_3_out, in_4);
  and and_2 (and_2_out, not_1_out, not_2_out, A0, in_4);
  LED led_2 (.in(and_2_out));
  and and_3 (and_3_out, not_1_out, A1, not_3_out, in_4);
  LED led_3 (.in(and_3_out));
  LED led_4 (.in(and_4_out));
  and and_4 (and_4_out, not_1_out, A1, A0, in_4);
  and and_5 (and_5_out, A2, not_2_out, not_3_out, in_4);
  LED led_5 (.in(and_5_out));
  LED led_6 (.in(and_6_out));
  and and_6 (and_6_out, A2, not_2_out, A0, in_4);
  and and_7 (and_7_out, A2, A1, not_3_out, in_4);
  LED led_7 (.in(and_7_out));
  and and_8 (and_8_out, A2, A1, A0, in_4);
  LED led_8 (.in(and_8_out));

  // Notes on the sheet:
  //   000
  //   001
  //   010
  //   011
  //   100
  //   101
  //   110
  //   111
endmodule
