// Logisim project 8-3_line_encoder.circ as structural Verilog: 1 circuit, main circuit main
module main (
  input  D0,
  input  D1,
  input  D2,
  input  D3,
  input  D4,
  input  D5,
  input  D6,
  input  D7
);

  wire or_1_out, or_2_out, or_3_out;

  or or_1 (or_1_out, D1, D3, D5, D7);
  or or_2 (or_2_out, D2, D3, D6, D7);
  or or_3 (or_3_out, D4, D5, D6, D7);
  LED led_1 (.in(or_1_out));
  LED led_2 (.in(or_2_out));
  LED led_3 (.in(or_3_out));

  // Notes on the sheet:
  //   A0
  //   A1
  //   A2
endmodule
